// Digital circuit design.dig as structural Verilog
module \design  (
  input  clk
);

  wire not_1_out, R_W;
  wire [7:0] D;
  wire [15:0] A;

  EEPROMDualPort #(.AddrBits(16), .Bits(8)) eepromdualport_1 (
    .A(A), .Din(D), .str(R_W), .C(clk), .ld(not_1_out), .D(D));
  not not_1 (not_1_out, R_W);
  a_risc a_risc_1 (.C(clk), .V(1'b1), .G(1'b0), .R(1'b0), .R_W(R_W), .D(D), .A(A));

  // Other names for the same wires on the sheet: C = clk

  // Notes on the sheet:
  //   clk: Hz: 16
  //   contents of eepromdualport_1 (hex, n*v repeats v):
  //   15,6,25,9,30,12,58,1e,e9,15,57,fffffffffffffff6
endmodule
